// Logisim project chandan_project_1.circ as structural Verilog: 15 circuits, main circuit Not_c
module Not_c (
  input  a,
  output Not_out
);

  nand nand_1 (Not_out, a, a);
endmodule

module And_c (
  input  a,
  input  b,
  output And_out
);

  wire nand_1_out;

  nand nand_1 (nand_1_out, a, b);
  Not_c not_c_1 (.a(nand_1_out), .Not_out(And_out));
endmodule

module Or_c (
  input  a,
  input  b,
  output Or_out
);

  wire nand_1_out, nand_2_out;

  nand nand_1 (nand_1_out, a, a);
  nand nand_2 (nand_2_out, b, b);
  nand nand_3 (Or_out, nand_1_out, nand_2_out);
endmodule

module Xor_c (
  input  a,
  input  b,
  output Xor_out
);

  wire and_c_1_and_out, and_c_2_and_out, not_c_1_not_out, not_c_2_not_out;

  Not_c not_c_1 (.a(a), .Not_out(not_c_1_not_out));
  Not_c not_c_2 (.a(b), .Not_out(not_c_2_not_out));
  And_c and_c_1 (.a(a), .b(not_c_2_not_out), .And_out(and_c_1_and_out));
  And_c and_c_2 (.a(not_c_1_not_out), .b(b), .And_out(and_c_2_and_out));
  Or_c or_c_1 (.a(and_c_1_and_out), .b(and_c_2_and_out), .Or_out(Xor_out));
endmodule

module Mux_c (
  input  sel,
  input  a,
  input  b,
  output Mux_out
);

  wire nand_1_out, nand_2_out, not_c_1_not_out;

  Not_c not_c_1 (.a(sel), .Not_out(not_c_1_not_out));
  nand nand_1 (nand_1_out, not_c_1_not_out, a);
  nand nand_2 (nand_2_out, sel, b);
  nand nand_3 (Mux_out, nand_1_out, nand_2_out);
endmodule

module DMux_c (
  input  sel,
  input  dmux_in,
  output a,
  output b
);

  wire nand_1_out, nand_2_out, not_c_1_not_out;

  Not_c not_c_1 (.a(sel), .Not_out(not_c_1_not_out));
  nand nand_1 (nand_1_out, not_c_1_not_out, dmux_in);
  nand nand_2 (nand_2_out, dmux_in, sel);
  Not_c not_c_2 (.a(nand_1_out), .Not_out(a));
  Not_c not_c_3 (.a(nand_2_out), .Not_out(b));
endmodule

module Not16_c (
  input  [15:0] Not16_in,
  output [15:0] Not16_out
);

  Not_c not_c_1 (.a(Not16_in[0]), .Not_out(Not16_out[0]));
  Not_c not_c_2 (.a(Not16_in[1]), .Not_out(Not16_out[1]));
  Not_c not_c_3 (.a(Not16_in[2]), .Not_out(Not16_out[2]));
  Not_c not_c_4 (.a(Not16_in[3]), .Not_out(Not16_out[3]));
  Not_c not_c_5 (.a(Not16_in[4]), .Not_out(Not16_out[4]));
  Not_c not_c_6 (.a(Not16_in[5]), .Not_out(Not16_out[5]));
  Not_c not_c_7 (.a(Not16_in[6]), .Not_out(Not16_out[6]));
  Not_c not_c_8 (.a(Not16_in[7]), .Not_out(Not16_out[7]));
  Not_c not_c_9 (.a(Not16_in[8]), .Not_out(Not16_out[8]));
  Not_c not_c_10 (.a(Not16_in[9]), .Not_out(Not16_out[9]));
  Not_c not_c_11 (.a(Not16_in[10]), .Not_out(Not16_out[10]));
  Not_c not_c_12 (.a(Not16_in[11]), .Not_out(Not16_out[11]));
  Not_c not_c_13 (.a(Not16_in[12]), .Not_out(Not16_out[12]));
  Not_c not_c_14 (.a(Not16_in[13]), .Not_out(Not16_out[13]));
  Not_c not_c_15 (.a(Not16_in[14]), .Not_out(Not16_out[14]));
  Not_c not_c_16 (.a(Not16_in[15]), .Not_out(Not16_out[15]));
endmodule

module And16_c (
  input  [15:0] And16_a,
  input  [15:0] And16_b,
  output [15:0] And16_out
);

  And_c and_c_1 (.a(And16_a[15]), .b(And16_b[15]), .And_out(And16_out[15]));
  And_c and_c_2 (.a(And16_a[13]), .b(And16_b[13]), .And_out(And16_out[13]));
  And_c and_c_3 (.a(And16_a[14]), .b(And16_b[14]), .And_out(And16_out[14]));
  And_c and_c_4 (.a(And16_a[12]), .b(And16_b[12]), .And_out(And16_out[12]));
  And_c and_c_5 (.a(And16_a[10]), .b(And16_b[10]), .And_out(And16_out[10]));
  And_c and_c_6 (.a(And16_a[11]), .b(And16_b[11]), .And_out(And16_out[11]));
  And_c and_c_7 (.a(And16_a[9]), .b(And16_b[9]), .And_out(And16_out[9]));
  And_c and_c_8 (.a(And16_a[7]), .b(And16_b[7]), .And_out(And16_out[7]));
  And_c and_c_9 (.a(And16_a[8]), .b(And16_b[8]), .And_out(And16_out[8]));
  And_c and_c_10 (.a(And16_a[5]), .b(And16_b[5]), .And_out(And16_out[5]));
  And_c and_c_11 (.a(And16_a[6]), .b(And16_b[6]), .And_out(And16_out[6]));
  And_c and_c_12 (.a(And16_a[4]), .b(And16_b[4]), .And_out(And16_out[4]));
  And_c and_c_13 (.a(And16_a[2]), .b(And16_b[2]), .And_out(And16_out[2]));
  And_c and_c_14 (.a(And16_a[3]), .b(And16_b[3]), .And_out(And16_out[3]));
  And_c and_c_15 (.a(And16_a[1]), .b(And16_b[1]), .And_out(And16_out[1]));
  And_c and_c_16 (.a(And16_a[0]), .b(And16_b[0]), .And_out(And16_out[0]));
endmodule

module Or16_c (
  input  [15:0] Or16_a,
  input  [15:0] Or16_b,
  output [15:0] Or16_out
);

  assign Or16_out = Or16_a | Or16_b;  // OR_Gate or_1, 16 bits wide
endmodule

module Mux16_c (
  input  [15:0] Mux16_a,
  input  [15:0] Mux16_b,
  input  sel,
  output [15:0] Mux16_out
);

  Multiplexer #(.width(16)) multiplexer_1 (.in0(Mux16_a), .in1(Mux16_b), .out(Mux16_out), .sel(sel));
endmodule

module Or8Way_c (
  input  [7:0] Or8Way_in,
  output Or8Way_out
);

  or or_1 (Or8Way_out, Or8Way_in[0], Or8Way_in[1], Or8Way_in[2], Or8Way_in[3], Or8Way_in[4], Or8Way_in[5], Or8Way_in[6], Or8Way_in[7]);
endmodule

module Mux4Way16_c (
  input  [1:0] sel,
  input  [15:0] a,
  input  [15:0] b,
  input  [15:0] c,
  input  [15:0] d,
  output [15:0] Mux4Way16_out
);

  wire [15:0] mux16_c_1_mux16_out, mux16_c_2_mux16_out;

  Mux16_c mux16_c_1 (.Mux16_a(a), .Mux16_b(b), .sel(sel[0]), .Mux16_out(mux16_c_1_mux16_out));
  Mux16_c mux16_c_2 (.Mux16_a(c), .Mux16_b(d), .sel(sel[0]), .Mux16_out(mux16_c_2_mux16_out));
  Mux16_c mux16_c_3 (
    .Mux16_a(mux16_c_1_mux16_out), .Mux16_b(mux16_c_2_mux16_out), .sel(sel[1]), .Mux16_out(Mux4Way16_out));
endmodule

module Mux8Way16_c (
  input  [2:0] sel,
  input  [15:0] a,
  input  [15:0] b,
  input  [15:0] c,
  input  [15:0] d,
  input  [15:0] e,
  input  [15:0] f,
  input  [15:0] g,
  input  [15:0] h,
  output [15:0] Mux8Way16_out
);

  wire [15:0] mux16_c_1_mux16_out, mux16_c_2_mux16_out, mux16_c_3_mux16_out, mux16_c_4_mux16_out,
       mux16_c_5_mux16_out, mux16_c_6_mux16_out;

  Mux16_c mux16_c_1 (.Mux16_a(e), .Mux16_b(f), .sel(sel[0]), .Mux16_out(mux16_c_1_mux16_out));
  Mux16_c mux16_c_2 (.Mux16_a(g), .Mux16_b(h), .sel(sel[0]), .Mux16_out(mux16_c_2_mux16_out));
  Mux16_c mux16_c_3 (.Mux16_a(c), .Mux16_b(d), .sel(sel[0]), .Mux16_out(mux16_c_3_mux16_out));
  Mux16_c mux16_c_4 (.Mux16_a(a), .Mux16_b(b), .sel(sel[0]), .Mux16_out(mux16_c_4_mux16_out));
  Mux16_c mux16_c_5 (
    .Mux16_a(mux16_c_1_mux16_out), .Mux16_b(mux16_c_2_mux16_out), .sel(sel[1]),
    .Mux16_out(mux16_c_5_mux16_out));
  Mux16_c mux16_c_6 (
    .Mux16_a(mux16_c_4_mux16_out), .Mux16_b(mux16_c_3_mux16_out), .sel(sel[1]),
    .Mux16_out(mux16_c_6_mux16_out));
  Mux16_c mux16_c_7 (
    .Mux16_a(mux16_c_6_mux16_out), .Mux16_b(mux16_c_5_mux16_out), .sel(sel[2]), .Mux16_out(Mux8Way16_out));
endmodule

module Dmux4Way_c (
  input  [1:0] sel,
  input  Dux4Way_in,
  output a,
  output b,
  output c,
  output d
);

  wire dmux_c_1_a, dmux_c_1_b;

  DMux_c dmux_c_1 (.dmux_in(Dux4Way_in), .sel(sel[1]), .a(dmux_c_1_a), .b(dmux_c_1_b));
  DMux_c dmux_c_2 (.dmux_in(dmux_c_1_a), .sel(sel[0]), .a(a), .b(b));
  DMux_c dmux_c_3 (.dmux_in(dmux_c_1_b), .sel(sel[0]), .a(c), .b(d));
endmodule

module DMux8Way_c (
  input  [2:0] sel,
  input  DMux8Way_in,
  output a,
  output b,
  output c,
  output d,
  output e,
  output f,
  output g,
  output h
);

  wire dmux_c_1_a, dmux_c_1_b, dmux_c_2_a, dmux_c_2_b, dmux_c_3_a, dmux_c_3_b;

  DMux_c dmux_c_1 (.dmux_in(DMux8Way_in), .sel(sel[2]), .a(dmux_c_1_a), .b(dmux_c_1_b));
  DMux_c dmux_c_2 (.dmux_in(dmux_c_1_a), .sel(sel[1]), .a(dmux_c_2_a), .b(dmux_c_2_b));
  DMux_c dmux_c_3 (.dmux_in(dmux_c_1_b), .sel(sel[1]), .a(dmux_c_3_a), .b(dmux_c_3_b));
  DMux_c dmux_c_4 (.dmux_in(dmux_c_2_a), .sel(sel[0]), .a(a), .b(b));
  DMux_c dmux_c_5 (.dmux_in(dmux_c_2_b), .sel(sel[0]), .a(c), .b(d));
  DMux_c dmux_c_6 (.dmux_in(dmux_c_3_a), .sel(sel[0]), .a(e), .b(f));
  DMux_c dmux_c_7 (.dmux_in(dmux_c_3_b), .sel(sel[0]), .a(g), .b(h));
endmodule
