// Logisim project chandan_project_2.circ as structural Verilog: 5 circuits, main circuit HalfAdder_c
module HalfAdder_c (
  input  a,
  input  b,
  output sum,
  output carry
);

  Xor_c xor_c_1 (.a(a), .b(b), .Xor_out(sum));
  And_c and_c_1 (.a(a), .b(b), .And_out(carry));
endmodule

module FullAdder_c (
  input  a,
  input  b,
  input  c,
  output sum,
  output carry
);

  wire halfadder_c_1_carry, halfadder_c_1_sum, halfadder_c_2_carry;

  HalfAdder_c halfadder_c_1 (.a(a), .b(b), .sum(halfadder_c_1_sum), .carry(halfadder_c_1_carry));
  HalfAdder_c halfadder_c_2 (.a(halfadder_c_1_sum), .b(c), .sum(sum), .carry(halfadder_c_2_carry));
  Or_c or_c_1 (.a(halfadder_c_2_carry), .b(halfadder_c_1_carry), .Or_out(carry));
endmodule

module Add16_c (
  input  [15:0] a,
  input  [15:0] b,
  output [15:0] Add16_out
);

  Adder #(.width(16)) adder_1 (.a(a), .b(b), .out(Add16_out));  // open: cin, cout
endmodule

module Inc16_c (
  input  [15:0] Inc_a,
  output [15:0] Inc_out
);

  Add16_c add16_c_1 (.a(Inc_a), .b(16'h1), .Add16_out(Inc_out));
endmodule

module ALU_c (
  input  zx,
  input  f,
  input  nx,
  input  zy,
  input  ny,
  input  no,
  input  [15:0] x,
  input  [15:0] y,
  output [15:0] ALU_out,
  output ng,
  output zr
);

  wire or8way_c_1_or8way_out, or8way_c_2_or8way_out, or_c_2_or_out;
  wire [15:0] add16_c_1_add16_out, and16_c_1_and16_out, mux16_c_1_mux16_out, mux16_c_2_mux16_out,
       mux16_c_3_mux16_out, mux16_c_4_mux16_out, mux16_c_5_mux16_out, not16_c_1_not16_out,
       not16_c_2_not16_out, not16_c_3_not16_out;

  Mux16_c mux16_c_1 (.Mux16_a(x), .Mux16_b({16{1'b0}}), .sel(zx), .Mux16_out(mux16_c_1_mux16_out));
  Not16_c not16_c_1 (.Not16_in(mux16_c_1_mux16_out), .Not16_out(not16_c_1_not16_out));
  Mux16_c mux16_c_2 (
    .Mux16_a(mux16_c_1_mux16_out), .Mux16_b(not16_c_1_not16_out), .sel(nx), .Mux16_out(mux16_c_2_mux16_out));
  Mux16_c mux16_c_3 (.Mux16_a(y), .Mux16_b({16{1'b0}}), .sel(zy), .Mux16_out(mux16_c_3_mux16_out));
  Mux16_c mux16_c_4 (
    .Mux16_a(mux16_c_3_mux16_out), .Mux16_b(not16_c_2_not16_out), .sel(ny), .Mux16_out(mux16_c_4_mux16_out));
  Not16_c not16_c_2 (.Not16_in(mux16_c_3_mux16_out), .Not16_out(not16_c_2_not16_out));
  And16_c and16_c_1 (.And16_a(mux16_c_2_mux16_out), .And16_b(mux16_c_4_mux16_out), .And16_out(and16_c_1_and16_out));
  Add16_c add16_c_1 (.a(mux16_c_2_mux16_out), .b(mux16_c_4_mux16_out), .Add16_out(add16_c_1_add16_out));
  Mux16_c mux16_c_5 (
    .Mux16_a(and16_c_1_and16_out), .Mux16_b(add16_c_1_add16_out), .sel(f), .Mux16_out(mux16_c_5_mux16_out));
  Not16_c not16_c_3 (.Not16_in(mux16_c_5_mux16_out), .Not16_out(not16_c_3_not16_out));
  Mux16_c mux16_c_6 (.Mux16_a(mux16_c_5_mux16_out), .Mux16_b(not16_c_3_not16_out), .sel(no), .Mux16_out(ALU_out));
  Or_c or_c_1 (.a(ALU_out[15]), .b(1'b0), .Or_out(ng));
  Or8Way_c or8way_c_1 (.Or8Way_in(ALU_out[15:8]), .Or8Way_out(or8way_c_1_or8way_out));
  Or8Way_c or8way_c_2 (.Or8Way_in(ALU_out[7:0]), .Or8Way_out(or8way_c_2_or8way_out));
  Or_c or_c_2 (.a(or8way_c_2_or8way_out), .b(or8way_c_1_or8way_out), .Or_out(or_c_2_or_out));
  Not_c not_c_1 (.a(or_c_2_or_out), .Not_out(zr));
endmodule
