// Logisim project chandan_project_3.circ as structural Verilog: 8 circuits, main circuit Bit_c
module Bit_c (
  input  load,
  input  Bit_in,
  output Bit_out
);

  wire clk, mux_c_1_mux_out;

  Clock u_clk (.out(clk));
  // Digital_Oscilloscope digital_oscilloscope_1: pin names not known; wires that end beside it: clk, Bit_in, load, Bit_out
  Mux_c mux_c_1 (.a(Bit_out), .b(Bit_in), .sel(load), .Mux_out(mux_c_1_mux_out));
  D_Flip_Flop d_ff_1 (.D(mux_c_1_mux_out), .clk(clk), .Q(Bit_out));  // open: Qn, preset, reset
endmodule

module Register_c (
  input  load,
  input  [15:0] Reg_in,
  output [15:0] Reg_out
);

  Bit_c bit_c_1 (.Bit_in(Reg_in[0]), .load(load), .Bit_out(Reg_out[0]));
  Bit_c bit_c_2 (.Bit_in(Reg_in[1]), .load(load), .Bit_out(Reg_out[1]));
  Bit_c bit_c_3 (.Bit_in(Reg_in[2]), .load(load), .Bit_out(Reg_out[2]));
  Bit_c bit_c_4 (.Bit_in(Reg_in[3]), .load(load), .Bit_out(Reg_out[3]));
  Bit_c bit_c_5 (.Bit_in(Reg_in[4]), .load(load), .Bit_out(Reg_out[4]));
  Bit_c bit_c_6 (.Bit_in(Reg_in[5]), .load(load), .Bit_out(Reg_out[5]));
  Bit_c bit_c_7 (.Bit_in(Reg_in[6]), .load(load), .Bit_out(Reg_out[6]));
  Bit_c bit_c_8 (.Bit_in(Reg_in[7]), .load(load), .Bit_out(Reg_out[7]));
  Bit_c bit_c_9 (.Bit_in(Reg_in[8]), .load(load), .Bit_out(Reg_out[8]));
  Bit_c bit_c_10 (.Bit_in(Reg_in[9]), .load(load), .Bit_out(Reg_out[9]));
  Bit_c bit_c_11 (.Bit_in(Reg_in[10]), .load(load), .Bit_out(Reg_out[10]));
  Bit_c bit_c_12 (.Bit_in(Reg_in[11]), .load(load), .Bit_out(Reg_out[11]));
  Bit_c bit_c_13 (.Bit_in(Reg_in[12]), .load(load), .Bit_out(Reg_out[12]));
  Bit_c bit_c_14 (.Bit_in(Reg_in[13]), .load(load), .Bit_out(Reg_out[13]));
  Bit_c bit_c_15 (.Bit_in(Reg_in[14]), .load(load), .Bit_out(Reg_out[14]));
  Bit_c bit_c_16 (.Bit_in(Reg_in[15]), .load(load), .Bit_out(Reg_out[15]));
endmodule

module RAM8_c (
  input  load,
  input  [2:0] address,
  input  [15:0] Ram_in,
  output [15:0] RAM8_out
);

  wire dmux8way_c_1_a, dmux8way_c_1_b, dmux8way_c_1_c, dmux8way_c_1_d, dmux8way_c_1_e, dmux8way_c_1_f,
       dmux8way_c_1_g, dmux8way_c_1_h;
  wire [15:0] register_c_1_reg_out, register_c_2_reg_out, register_c_3_reg_out, register_c_4_reg_out,
       register_c_5_reg_out, register_c_6_reg_out, register_c_7_reg_out, register_c_8_reg_out;

  DMux8Way_c dmux8way_c_1 (
    .DMux8Way_in(load), .sel(address), .a(dmux8way_c_1_a), .b(dmux8way_c_1_b), .c(dmux8way_c_1_c),
    .d(dmux8way_c_1_d), .e(dmux8way_c_1_e), .f(dmux8way_c_1_f), .g(dmux8way_c_1_g), .h(dmux8way_c_1_h));
  Register_c register_c_1 (.Reg_in(Ram_in), .load(dmux8way_c_1_a), .Reg_out(register_c_1_reg_out));
  Register_c register_c_2 (.Reg_in(Ram_in), .load(dmux8way_c_1_b), .Reg_out(register_c_2_reg_out));
  Register_c register_c_3 (.Reg_in(Ram_in), .load(dmux8way_c_1_c), .Reg_out(register_c_3_reg_out));
  Register_c register_c_4 (.Reg_in(Ram_in), .load(dmux8way_c_1_d), .Reg_out(register_c_4_reg_out));
  Register_c register_c_5 (.Reg_in(Ram_in), .load(dmux8way_c_1_e), .Reg_out(register_c_5_reg_out));
  Register_c register_c_6 (.Reg_in(Ram_in), .load(dmux8way_c_1_f), .Reg_out(register_c_6_reg_out));
  Register_c register_c_7 (.Reg_in(Ram_in), .load(dmux8way_c_1_g), .Reg_out(register_c_7_reg_out));
  Register_c register_c_8 (.Reg_in(Ram_in), .load(dmux8way_c_1_h), .Reg_out(register_c_8_reg_out));
  Mux8Way16_c mux8way16_c_1 (
    .a(register_c_1_reg_out), .b(register_c_2_reg_out), .c(register_c_3_reg_out), .d(register_c_4_reg_out),
    .e(register_c_5_reg_out), .f(register_c_6_reg_out), .g(register_c_7_reg_out), .h(register_c_8_reg_out),
    .sel(address), .Mux8Way16_out(RAM8_out));
endmodule

module RAM64_c (
  input  load,
  input  [5:0] address,
  input  [15:0] RAM64_in,
  output [15:0] RAM64_out
);

  wire dmux8way_c_1_a, dmux8way_c_1_b, dmux8way_c_1_c, dmux8way_c_1_d, dmux8way_c_1_e, dmux8way_c_1_f,
       dmux8way_c_1_g, dmux8way_c_1_h;
  wire [15:0] ram8_c_1_ram8_out, ram8_c_2_ram8_out, ram8_c_3_ram8_out, ram8_c_4_ram8_out, ram8_c_5_ram8_out,
       ram8_c_6_ram8_out, ram8_c_7_ram8_out, ram8_c_8_ram8_out;

  DMux8Way_c dmux8way_c_1 (
    .DMux8Way_in(load), .sel(address[2:0]), .a(dmux8way_c_1_a), .b(dmux8way_c_1_b), .c(dmux8way_c_1_c),
    .d(dmux8way_c_1_d), .e(dmux8way_c_1_e), .f(dmux8way_c_1_f), .g(dmux8way_c_1_g), .h(dmux8way_c_1_h));
  RAM8_c ram8_c_1 (.address(address[5:3]), .Ram_in(RAM64_in), .load(dmux8way_c_1_a), .RAM8_out(ram8_c_1_ram8_out));
  RAM8_c ram8_c_2 (.address(address[5:3]), .Ram_in(RAM64_in), .load(dmux8way_c_1_b), .RAM8_out(ram8_c_2_ram8_out));
  RAM8_c ram8_c_3 (.address(address[5:3]), .Ram_in(RAM64_in), .load(dmux8way_c_1_c), .RAM8_out(ram8_c_3_ram8_out));
  RAM8_c ram8_c_4 (.address(address[5:3]), .Ram_in(RAM64_in), .load(dmux8way_c_1_d), .RAM8_out(ram8_c_4_ram8_out));
  RAM8_c ram8_c_5 (.address(address[5:3]), .Ram_in(RAM64_in), .load(dmux8way_c_1_e), .RAM8_out(ram8_c_5_ram8_out));
  RAM8_c ram8_c_6 (.address(address[5:3]), .Ram_in(RAM64_in), .load(dmux8way_c_1_f), .RAM8_out(ram8_c_6_ram8_out));
  RAM8_c ram8_c_7 (.address(address[5:3]), .Ram_in(RAM64_in), .load(dmux8way_c_1_g), .RAM8_out(ram8_c_7_ram8_out));
  RAM8_c ram8_c_8 (.address(address[5:3]), .Ram_in(RAM64_in), .load(dmux8way_c_1_h), .RAM8_out(ram8_c_8_ram8_out));
  Mux8Way16_c mux8way16_c_1 (
    .a(ram8_c_1_ram8_out), .b(ram8_c_2_ram8_out), .c(ram8_c_3_ram8_out), .d(ram8_c_4_ram8_out),
    .e(ram8_c_5_ram8_out), .f(ram8_c_6_ram8_out), .g(ram8_c_7_ram8_out), .h(ram8_c_8_ram8_out),
    .sel(address[2:0]), .Mux8Way16_out(RAM64_out));
endmodule

module RAM512_c (
  input  [8:0] address,
  input  load,
  input  [15:0] RAM512_in,
  output [15:0] RAM15_out
);

  wire clock_1_out;

  Clock clock_1 (.out(clock_1_out));
  RAM #(.addrWidth(9), .dataWidth(16)) ram_1 (
    .addr(address), .we(load), .oe(1'b1), .clk(clock_1_out), .din(RAM512_in), .dout(RAM15_out));
endmodule

module RAM4K_c (
  input  [11:0] address,
  input  load,
  input  [15:0] RAM4K_in,
  output [15:0] RAM4K_out
);

  wire clock_1_out;

  Clock clock_1 (.out(clock_1_out));
  RAM #(.addrWidth(12), .dataWidth(16)) ram_1 (
    .addr(address), .we(load), .oe(1'b1), .clk(clock_1_out), .din(RAM4K_in), .dout(RAM4K_out));
endmodule

module RAM16K_c (
  input  [13:0] address,
  input  load,
  input  [15:0] RAM16K_in,
  output [15:0] RAM16K_out
);

  wire clock_1_out;

  Clock clock_1 (.out(clock_1_out));
  RAM #(.addrWidth(14), .dataWidth(16)) ram_1 (
    .addr(address), .we(load), .oe(1'b1), .clk(clock_1_out), .din(RAM16K_in), .dout(RAM16K_out));
endmodule

module PC_c (
  input  [15:0] PC_in,
  input  inc,
  input  load,
  input  reset,
  output [15:0] PC_out
);

  wire [15:0] inc16_c_1_inc_out, mux8way16_c_1_mux8way16_out;

  Register_c register_c_1 (.Reg_in(mux8way16_c_1_mux8way16_out), .load(1'b1), .Reg_out(PC_out));
  Inc16_c inc16_c_1 (.Inc_a(PC_out), .Inc_out(inc16_c_1_inc_out));
  Mux8Way16_c mux8way16_c_1 (
    .a(PC_out), .b(inc16_c_1_inc_out), .c(PC_in), .d(PC_in), .e({16{1'b0}}), .f({16{1'b0}}), .g({16{1'b0}}),
    .h({16{1'b0}}), .sel({reset, load, inc}), .Mux8Way16_out(mux8way16_c_1_mux8way16_out));
endmodule
